# Fritzing sketch main (saved by Fritzing 0.9.6b)
breadboards: 2

parts:
  R1 = Resistor [tolerance=±5% power=0.25 resistance=220 package=THT]
  R2 = Resistor [tolerance=±5% power=0.25 resistance=220 package=THT]
  R3 = Resistor [tolerance=±5% power=0.25 resistance=220 package=THT]
  R4 = Resistor [tolerance=±5% power=0.25 resistance=220 package=THT]
  R5 = Resistor [tolerance=±5% power=0.25 resistance=220 package=THT]
  R6 = Resistor [tolerance=±5% power=0.25 resistance=220 package=THT]
  R7 = Resistor [tolerance=±5% power=0.25 resistance=220 package=THT]
  PIC_16F877A1 = PIC 16F877A [package=THT]
  C1 = Ceramic Capacitor [capacitance=100nF voltage=35V package="100 mil [THT, multilayer]"]
  R8 = Rotary Potentiometer (Large) [maximum_resistance=10kΩ package=THT]
  U1 = 7-SEGMENT-DISPLAY [package=7-segment-display]
  U2 = 7-SEGMENT-DISPLAY [package=7-segment-display]
  R9 = Resistor [tolerance=±5% power=0.25 resistance=220 package=THT]
  R10 = Resistor [tolerance=±5% power=0.25 resistance=220 package=THT]
  R11 = Resistor [tolerance=±5% power=0.25 resistance=220 package=THT]
  R12 = Resistor [tolerance=±5% power=0.25 resistance=220 package=THT]
  R13 = Resistor [tolerance=±5% power=0.25 resistance=220 package=THT]
  R14 = Resistor [tolerance=±5% power=0.25 resistance=220 package=THT]
  R15 = Resistor [tolerance=±5% power=0.25 resistance=220 package=THT]
  R16 = Resistor [tolerance=±5% power=0.25 resistance=220 package=THT]

nets:
  N1: R1.Pin_0, PIC_16F877A1.RB7
  N2: R1.Pin_1, U1.G2
  N3: R2.Pin_0, PIC_16F877A1.RB6
  N4: R2.Pin_1, U1.A
  N5: R3.Pin_0, PIC_16F877A1.RB5
  N6: R3.Pin_1, U1.DP
  N7: R4.Pin_0, PIC_16F877A1.RB4
  N8: R4.Pin_1, U1.G1
  N9: R5.Pin_0, PIC_16F877A1.RB3
  N10: R5.Pin_1, U1.D
  N11: R6.Pin_0, PIC_16F877A1.RB2
  N12: R6.Pin_1, U1.G
  N13: R7.Pin_0, PIC_16F877A1.RB1
  N14: R7.Pin_1, U1.E
  N15: PIC_16F877A1.RA0/AN0, C1.1, R8.wiper
  N16: PIC_16F877A1.RC1, R10.Pin_0
  N17: PIC_16F877A1.RC2, R11.Pin_0
  N18: PIC_16F877A1.RC3, R12.Pin_0
  N19: PIC_16F877A1.RC4, R13.Pin_0
  N20: PIC_16F877A1.RC5, R14.Pin_0
  N21: PIC_16F877A1.RC6/TX/CK, R15.Pin_0
  N22: PIC_16F877A1.RC7/RX/DT, R16.Pin_0
  N23: PIC_16F877A1.VSS#30, C1.0, R8.leg2, U1.C, U2.C
  N24: PIC_16F877A1.VDD#31, R8.leg1, R9.Pin_0
  N25: U1.B, R9.Pin_1
  N26: U2.E, R10.Pin_1
  N27: U2.D, R12.Pin_1
  N28: U2.G1, R13.Pin_1
  N29: U2.DP, R14.Pin_1
  N30: U2.A, R15.Pin_1
  N31: U2.G2, R16.Pin_1
  N32: U2.G, R11.Pin_1
